// Logisim project counter.circ as structural Verilog: 6 circuits, main circuit main
module main (
  output Q1,
  output Q2,
  output Q3,
  output Q4,
  output Q5
);

  wire and_1_out, clock_1_out, d_trigger_1_q, d_trigger_2_q, d_trigger_3_q, d_trigger_4_q, d_trigger_5_q,
       not_1_out, not_2_out, not_3_out, not_4_out, not_5_out, sum_one_1_h, sum_one_2_h, sum_one_3_h,
       sum_one_4_h;

  Clock clock_1 (.out(clock_1_out));
  D_Trigger d_trigger_1 (.D(1'b1), .C(clock_1_out), .W(clock_1_out), .Wc(and_1_out), .Q(d_trigger_1_q));
  D_Trigger d_trigger_2 (.D(1'b0), .C(d_trigger_1_q), .W(clock_1_out), .Wc(and_1_out), .Q(d_trigger_2_q));
  D_Trigger d_trigger_3 (.D(1'b0), .C(d_trigger_2_q), .W(clock_1_out), .Wc(and_1_out), .Q(d_trigger_3_q));
  D_Trigger d_trigger_4 (.D(1'b1), .C(d_trigger_3_q), .W(clock_1_out), .Wc(and_1_out), .Q(d_trigger_4_q));
  D_Trigger d_trigger_5 (.D(1'b0), .C(d_trigger_4_q), .W(clock_1_out), .Wc(and_1_out), .Q(d_trigger_5_q));
  not not_1 (not_1_out, d_trigger_1_q);
  not not_2 (not_2_out, d_trigger_2_q);
  not not_3 (not_3_out, d_trigger_3_q);
  not not_4 (not_4_out, d_trigger_4_q);
  not not_5 (not_5_out, d_trigger_5_q);
  Sum_One sum_one_1 (.X(1'b1), .Y(not_1_out), .Z(Q1), .H(sum_one_1_h));
  Sum_One sum_one_2 (.X(sum_one_1_h), .Y(not_2_out), .Z(Q2), .H(sum_one_2_h));
  Sum_One sum_one_3 (.X(sum_one_2_h), .Y(not_3_out), .Z(Q3), .H(sum_one_3_h));
  Sum_One sum_one_4 (.X(sum_one_3_h), .Y(not_4_out), .Z(Q4), .H(sum_one_4_h));
  Sum_One sum_one_5 (.X(sum_one_4_h), .Y(not_5_out), .Z(Q5));  // open: H
  and and_1 (and_1_out, not_1_out, not_2_out, not_2_out, not_4_out, not_5_out);
endmodule

module RS_TRIGER (
  input  S,
  input  C,
  input  R,
  output Q,
  output nQ
);

  wire and_1_out, and_2_out, nor_1_out, por_1_out;

  and and_1 (and_1_out, S, C);
  and and_2 (and_2_out, C, R);
  POR por_1 (.out(por_1_out));
  nor nor_1 (nor_1_out, and_1_out, Q);
  nor nor_2 (Q, nQ, and_2_out);
  or or_1 (nQ, por_1_out, nor_1_out);
endmodule

module JK_Trigger (
  input  J,
  input  C,
  input  K,
  output Q,
  output nQ
);

  wire and_1_out, and_2_out, not_1_out, rs_triger_1_nq, rs_triger_1_q;

  and and_1 (and_1_out, nQ, J);
  and and_2 (and_2_out, K, Q);
  RS_TRIGER rs_triger_1 (.S(and_1_out), .C(C), .R(and_2_out), .Q(rs_triger_1_q), .nQ(rs_triger_1_nq));
  not not_1 (not_1_out, C);
  RS_TRIGER rs_triger_2 (.S(rs_triger_1_q), .C(not_1_out), .R(rs_triger_1_nq), .Q(Q), .nQ(nQ));
endmodule

module D_Trigger (
  input  D,
  input  C,
  input  W,
  input  Wc,
  output Q
);

  wire jk_trigger_1_nq, mult_1_y, mult_2_y, not_1_out;

  Mult mult_1 (.A(Wc), .X0(jk_trigger_1_nq), .X1(D), .Y(mult_1_y));
  Mult mult_2 (.A(Wc), .X0(C), .X1(W), .Y(mult_2_y));
  not not_1 (not_1_out, mult_1_y);
  JK_Trigger jk_trigger_1 (.J(mult_1_y), .C(mult_2_y), .K(not_1_out), .Q(Q), .nQ(jk_trigger_1_nq));
endmodule

module Mult (
  input  A,
  input  X0,
  input  X1,
  output Y
);

  wire and_1_out, and_2_out, not_1_out;

  not not_1 (not_1_out, A);
  and and_1 (and_1_out, not_1_out, X0);
  and and_2 (and_2_out, A, X1);
  or or_1 (Y, and_1_out, and_2_out);
endmodule

module Sum_One (
  input  X,
  input  Y,
  output Z,
  output H
);

  xor xor_1 (Z, X, Y);
  and and_1 (H, X, Y);
endmodule
