// Logisim project lfsr.circ as structural Verilog: 4 circuits, main circuit main
module main (
  input  PowerOnReset,
  output out_2
);

  wire clock_1_out, N1_q, N2_q, N3_q, N4_q, N5_q, N6_q, N7_q, N8_q, N9_q, N10_q, N11_q, N12_q, N13_q, N14_q,
       N15_q, N16_q, or_1_out, or_2_out, xor_1_out, xor_2_out, xor_3_out, xor_4_out;

  Clock clock_1 (.out(clock_1_out));
  D_Trigger N16 (.C(clock_1_out), .D(out_2), .Q(N16_q));
  xor xor_1 (xor_1_out, out_2, N16_q);
  D_Trigger N15 (.C(clock_1_out), .D(xor_1_out), .Q(N15_q));
  D_Trigger N14 (.C(clock_1_out), .D(N15_q), .Q(N14_q));
  xor xor_2 (xor_2_out, out_2, N14_q);
  D_Trigger N13 (.C(clock_1_out), .D(xor_2_out), .Q(N13_q));
  xor xor_3 (xor_3_out, out_2, N13_q);
  D_Trigger N12 (.C(clock_1_out), .D(xor_3_out), .Q(N12_q));
  xor xor_4 (xor_4_out, out_2, N11_q);
  D_Trigger N11 (.C(clock_1_out), .D(N12_q), .Q(N11_q));
  D_Trigger N10 (.C(clock_1_out), .D(xor_4_out), .Q(N10_q));
  D_Trigger N9 (.C(clock_1_out), .D(N10_q), .Q(N9_q));
  D_Trigger N8 (.C(clock_1_out), .D(N9_q), .Q(N8_q));
  D_Trigger N7 (.C(clock_1_out), .D(N8_q), .Q(N7_q));
  D_Trigger N6 (.C(clock_1_out), .D(N7_q), .Q(N6_q));
  D_Trigger N5 (.C(clock_1_out), .D(N6_q), .Q(N5_q));
  D_Trigger N4 (.C(clock_1_out), .D(N5_q), .Q(N4_q));
  D_Trigger N3 (.C(clock_1_out), .D(N4_q), .Q(N3_q));
  D_Trigger N2 (.C(clock_1_out), .D(N3_q), .Q(N2_q));
  or or_1 (or_1_out, PowerOnReset, N1_q);
  D_Trigger N1 (.C(clock_1_out), .D(N2_q), .Q(N1_q));
  D_Trigger N0 (.C(or_2_out), .D(or_1_out), .Q(out_2));
  or or_2 (or_2_out, PowerOnReset, clock_1_out);
endmodule

module RS_TRIGER (
  input  S,
  input  C,
  input  R,
  output Q,
  output nQ
);

  wire and_1_out, and_2_out, nor_1_out, por_1_out;

  and and_1 (and_1_out, S, C);
  and and_2 (and_2_out, C, R);
  POR por_1 (.out(por_1_out));
  nor nor_1 (nor_1_out, and_1_out, Q);
  nor nor_2 (Q, nQ, and_2_out);
  or or_1 (nQ, por_1_out, nor_1_out);
endmodule

module JK_Trigger (
  input  J,
  input  C,
  input  K,
  output Q,
  output nQ
);

  wire and_1_out, and_2_out, not_1_out, rs_triger_1_nq, rs_triger_1_q;

  and and_1 (and_1_out, nQ, J);
  and and_2 (and_2_out, K, Q);
  RS_TRIGER rs_triger_1 (.S(and_1_out), .C(C), .R(and_2_out), .Q(rs_triger_1_q), .nQ(rs_triger_1_nq));
  not not_1 (not_1_out, C);
  RS_TRIGER rs_triger_2 (.S(rs_triger_1_q), .C(not_1_out), .R(rs_triger_1_nq), .Q(Q), .nQ(nQ));
endmodule

module D_Trigger (
  input  D,
  input  C,
  output Q
);

  wire not_1_out;

  not not_1 (not_1_out, D);
  JK_Trigger jk_trigger_1 (.J(D), .C(C), .K(not_1_out), .Q(Q));  // open: nQ
endmodule
